# Fritzing sketch Compact Passive MSF Antenna (saved by Fritzing 0.9.8b)
circuit board: 1.33401cm x 0.902479cm
breadboards: 1

parts:
  MCU1 = Raspberry Pi Zero
  10K = Resistor [tolerance=±5% resistance=10k power=0.25 package="1206 [SMD]"]
  MSF = Inductor [package="400 mil [THT]"]

nets:
  N1: MCU1.pin_7, 10K.Pin_1
  N2: MCU1.pin_9, MSF.pin_0
  N3: 10K.Pin_0, MSF.pin_1

notes:
  1
  3
  9
