# Fritzing sketch Passive MSF60 Antenna (saved by Fritzing 0.9.8b)
circuit board: 6.40211cm x 2.93992cm
breadboards: 1

parts:
  MCU1 = Raspberry Pi Zero
  ANTENNA = Inductor [package="400 mil [THT]"]
  10K = Resistor [tolerance=±5% power=0.25 resistance=10k package=THT]

nets:
  N1: MCU1.pin_6, MCU1.pin_25, MCU1.pin_30, ANTENNA.pin_0
  N2: MCU1.pin_7, 10K.Pin_1
  N3: ANTENNA.pin_1, 10K.Pin_0

notes:
  github.com/GOTO-GOSUB
  github.com/hzeller/txtempus
  TXTEMPUS MSF 60KHZ ANTENNA
